# Fritzing sketch LED_bike_remote (saved by Fritzing 0.9.4)
breadboards: 1

parts:
  S1 = Pushbutton [package="[THT]"]
  Part2 = Arduino Nano (Rev3.0) (ICSP)
  LED1 = smd LED [color="Yellow (585nm)" package="0805 [SMD]"]
  R2 = Resistor [tolerance=±5% resistance=220 package=THT]
  S2 = Pushbutton [package="[THT]"]
  R3 = Resistor [tolerance=±5% resistance=100 package=THT]
  R4 = Resistor [tolerance=±5% resistance=220 package=THT]
  LED2 = smd LED [color="Yellow (585nm)" package="0805 [SMD]"]
  R1 = Resistor [tolerance=±5% resistance=100 package=THT]
  S4 = Toggle Switch [package=THT]
  R5 = Resistor [tolerance=±5% resistance=100 package=THT]
  C1 = Capacitor Polarized [package=panasonic_c]
  Part4 = Bluetooth HC-05 Macho
  VCC1 = Battery block 9V
  Part5 = InvenSense MPU6050

nets:
  N1: S1.Pin_1, S1.Pin_2, Part2.D3, R1.Pin_0
  VCC: S1.Pin_3, S1.Pin_4, Part2.VIN, S2.Pin_3, S2.Pin_4, S4.COM, C1.+, Part4.VCC, Part5.VCC
  N2: Part2.D1/TX, Part4.RXD
  N3: Part2.D0/RX, Part4.TXD
  N4: Part2.D2, Part5.INT
  N5: Part2.D4, S2.Pin_1, S2.Pin_2, R3.Pin_0
  N6: Part2.D6, LED1.anode
  N7: Part2.D7, LED2.anode
  N8: Part2.A5, Part5.SCL
  N9: Part2.A4, Part5.SDA
  N10: LED1.cathode, R2.Pin_0
  GND: R2.Pin_1, R3.Pin_1, R4.Pin_1, R1.Pin_1, R5.Pin_1, C1.-, Part4.GND, VCC1.-, Part5.GND
  N11: R4.Pin_0, LED2.cathode
  N12: S4.L1, VCC1.+
  N13: S4.L2, R5.Pin_0
